# Fritzing sketch week6_class_circuit (saved by Fritzing 1.0.8)
breadboards: 1

parts:
  U1 = Breadboard Power Supply Board SMD
  R1 = Resistor [resistance=1k tolerance=±5% power=0.25W package=THT]
  LED1 = LED - 5mm [color="Yellow (585nm)" current=0.030A package="5 mm [THT]"]
  S1 = Pushbutton [package="[THT]"]
  R2 = Resistor [resistance=1k tolerance=±5% power=0.25W package=THT]
  LED2 = LED - 5mm [color="Blue (470nm)" current=0.030A package="5 mm [THT]"]

nets:
  N1: U1.GND, LED1.cathode, LED2.cathode
  N2: U1.VCC, R1.Pin_1, S1.Pin_1, S1.Pin_2
  N3: R1.Pin_0, LED1.anode
  N4: S1.Pin_3, S1.Pin_4, R2.Pin_1
  N5: R2.Pin_0, LED2.anode
